// Logisim project f3&f5.circ as structural Verilog: 45 circuits, main circuit main
module main (
  input  \多路选择器_7段数码管演示 ,
  input  in_2,
  input  in_3,
  input  in_4,
  input  in_5,
  input  \D锁存器演示 ,
  input  in_7,
  input  in_8,
  input  \D触发器演示 ,
  input  in_10,
  input  in_11,
  input  in_12,
  input  in_13,
  input  in_14,
  input  in_15,
  output out_16,
  output out_17
);

  wire add_sm4_1_r0, add_sm4_1_r1, add_sm4_1_r2, add_sm4_1_r3, add_sm4_1_sgn, adder4_1_c, adder4_1_s0,
       adder4_1_s1, adder4_1_s2, adder4_1_s3, comparer_4_1_o, d_latch_1_not_q, d_trigger_1_not_q,
       dipswitch_2_p1, dipswitch_2_p2, dipswitch_2_p3, dipswitch_2_p4, dipswitch_2_p5, dipswitch_2_p6,
       dipswitch_2_p7, dipswitch_2_p8, dipswitch_3_p1, dipswitch_3_p2, dipswitch_3_p3, dipswitch_3_p4,
       dipswitch_4_p1, dipswitch_4_p2, dipswitch_4_p3, dipswitch_4_p4, dipswitch_4_p5, dipswitch_5_p1,
       dipswitch_5_p2, dipswitch_5_p3, dipswitch_5_p4, dipswitch_5_p5, dipswitch_5_p6, dipswitch_5_p7,
       dipswitch_5_p8, dipswitch_6_p1, dipswitch_6_p2, dipswitch_7_p1, dipswitch_7_p2, dipswitch_7_p3,
       dipswitch_7_p4, dipswitch_7_p5, dipswitch_7_p6, reg4_1_q0, reg4_1_q1, reg4_1_q2, reg4_1_q3,
       seg7sel_1_a, seg7sel_1_h, seg7sel_1_out_7, seg7sel_1_out_8, seg7sel_1_out_9, seg7sel_1_out_10,
       seg7sel_1_out_11, seg7sel_1_out_12, seg7sel_2_a, seg7sel_2_h, seg7sel_2_out_7, seg7sel_2_out_8,
       seg7sel_2_out_9, seg7sel_2_out_10, seg7sel_2_out_11, seg7sel_2_out_12, seg7sel_3_a, seg7sel_3_h,
       seg7sel_3_out_7, seg7sel_3_out_8, seg7sel_3_out_9, seg7sel_3_out_10, seg7sel_3_out_11,
       seg7sel_3_out_12, seg7sel_4_a, seg7sel_4_h, seg7sel_4_out_7, seg7sel_4_out_8, seg7sel_4_out_9,
       seg7sel_4_out_10, seg7sel_4_out_11, seg7sel_4_out_12, seg7sel_5_a, seg7sel_5_h, seg7sel_5_out_7,
       seg7sel_5_out_8, seg7sel_5_out_9, seg7sel_5_out_10, seg7sel_5_out_11, seg7sel_5_out_12, suber4_1_d0,
       suber4_1_d1, suber4_1_d2, suber4_1_d3, suber4_1_lh;

  // DipSwitch dipswitch_1: pin names not known
  // DipSwitch dipswitch_2: pin names not known; wires that end beside it: dipswitch_2_p1, dipswitch_2_p2, dipswitch_2_p3, dipswitch_2_p4, dipswitch_2_p5, dipswitch_2_p6, dipswitch_2_p7, dipswitch_2_p8
  // DipSwitch dipswitch_3: pin names not known; wires that end beside it: dipswitch_3_p1, dipswitch_3_p2, dipswitch_3_p3, dipswitch_3_p4
  // DipSwitch dipswitch_4: pin names not known; wires that end beside it: dipswitch_4_p1, dipswitch_4_p2, dipswitch_4_p3, dipswitch_4_p4, dipswitch_4_p5
  // DipSwitch dipswitch_5: pin names not known; wires that end beside it: dipswitch_5_p1, dipswitch_5_p2, dipswitch_5_p3, dipswitch_5_p4, dipswitch_5_p5, dipswitch_5_p6, dipswitch_5_p7, dipswitch_5_p8
  D_trigger d_trigger_1 (.R(\D触发器演示 ), .clk(in_11), .D(d_trigger_1_not_q), .Q(out_17), .not_Q(d_trigger_1_not_q));
  seg7sel seg7sel_1 (
    .D3(\多路选择器_7段数码管演示 ), .D2(in_2), .D1(in_3), .D0(in_4), .is_hex(in_5), .a(seg7sel_1_a),
    .out_7(seg7sel_1_out_7), .out_8(seg7sel_1_out_8), .out_9(seg7sel_1_out_9), .out_10(seg7sel_1_out_10),
    .out_11(seg7sel_1_out_11), .out_12(seg7sel_1_out_12), .h(seg7sel_1_h));
  LED led_1 (.in(comparer_4_1_o));
  comparer_4 comparer_4_1 (
    .a3(dipswitch_2_p1), .a2(dipswitch_2_p2), .a1(dipswitch_2_p3), .a0(dipswitch_2_p4), .b3(dipswitch_2_p5),
    .b2(dipswitch_2_p6), .b1(dipswitch_2_p7), .b0(dipswitch_2_p8), .o(comparer_4_1_o));
  LED led_2 (.in(adder4_1_c));
  adder4 adder4_1 (
    .a3(dipswitch_3_p1), .a2(dipswitch_3_p2), .a1(dipswitch_3_p3), .a0(dipswitch_3_p4), .b3(dipswitch_4_p1),
    .b2(dipswitch_4_p2), .b1(dipswitch_4_p3), .b0(dipswitch_4_p4), .carry(dipswitch_4_p5), .C(adder4_1_c),
    .S3(adder4_1_s3), .S2(adder4_1_s2), .S1(adder4_1_s1), .S0(adder4_1_s0));
  add_sm4 add_sm4_1 (
    .A13(dipswitch_5_p1), .A12(dipswitch_5_p2), .A11(dipswitch_5_p3), .A10(dipswitch_5_p4),
    .A23(dipswitch_5_p5), .A22(dipswitch_5_p6), .A21(dipswitch_5_p7), .A20(dipswitch_5_p8),
    .SGN(add_sm4_1_sgn), .R3(add_sm4_1_r3), .R2(add_sm4_1_r2), .R1(add_sm4_1_r1), .R0(add_sm4_1_r0));
  _7_Segment_Display u_7_segment_display_1 (
    .g(seg7sel_1_out_12), .f(seg7sel_1_out_11), .a(seg7sel_1_a), .b(seg7sel_1_out_7), .e(seg7sel_1_out_10),
    .d(seg7sel_1_out_9), .c(seg7sel_1_out_8), .dp(seg7sel_1_h));
  // DipSwitch dipswitch_6: pin names not known; wires that end beside it: dipswitch_6_p1, dipswitch_6_p2
  // DipSwitch dipswitch_7: pin names not known; wires that end beside it: dipswitch_7_p1, dipswitch_7_p2, dipswitch_7_p3, dipswitch_7_p4, dipswitch_7_p5, dipswitch_7_p6
  seg7sel seg7sel_2 (
    .D3(adder4_1_s3), .D2(adder4_1_s2), .D1(adder4_1_s1), .D0(adder4_1_s0), .is_hex(1'b1), .a(seg7sel_2_a),
    .out_7(seg7sel_2_out_7), .out_8(seg7sel_2_out_8), .out_9(seg7sel_2_out_9), .out_10(seg7sel_2_out_10),
    .out_11(seg7sel_2_out_11), .out_12(seg7sel_2_out_12), .h(seg7sel_2_h));
  seg7sel seg7sel_3 (
    .D3(add_sm4_1_r3), .D2(add_sm4_1_r2), .D1(add_sm4_1_r1), .D0(add_sm4_1_r0), .is_hex(1'b1),
    .a(seg7sel_3_a), .out_7(seg7sel_3_out_7), .out_8(seg7sel_3_out_8), .out_9(seg7sel_3_out_9),
    .out_10(seg7sel_3_out_10), .out_11(seg7sel_3_out_11), .out_12(seg7sel_3_out_12), .h(seg7sel_3_h));
  _7_Segment_Display u_7_segment_display_2 (.g(add_sm4_1_sgn));  // open: f, a, b, e, d, c, dp
  LED led_3 (.in(suber4_1_lh));
  suber4 suber4_1 (
    .SD3(dipswitch_6_p1), .SD2(dipswitch_6_p2), .SD1(dipswitch_7_p1), .SD0(dipswitch_7_p2),
    .SR3(dipswitch_7_p3), .SR2(dipswitch_7_p4), .SR1(dipswitch_7_p5), .SR0(dipswitch_7_p6), .LH(suber4_1_lh),
    .D3(suber4_1_d3), .D2(suber4_1_d2), .D1(suber4_1_d1), .D0(suber4_1_d0));  // open: LL
  _7_Segment_Display u_7_segment_display_3 (
    .g(seg7sel_2_out_12), .f(seg7sel_2_out_11), .a(seg7sel_2_a), .b(seg7sel_2_out_7), .e(seg7sel_2_out_10),
    .d(seg7sel_2_out_9), .c(seg7sel_2_out_8), .dp(seg7sel_2_h));
  _7_Segment_Display u_7_segment_display_4 (
    .g(seg7sel_3_out_12), .f(seg7sel_3_out_11), .a(seg7sel_3_a), .b(seg7sel_3_out_7), .e(seg7sel_3_out_10),
    .d(seg7sel_3_out_9), .c(seg7sel_3_out_8), .dp(seg7sel_3_h));
  reg4 reg4_1 (
    .R(in_8), .clk(in_10), .EN(1'b1), .D3(in_12), .D2(in_13), .D1(in_14), .D0(in_15), .Q3(reg4_1_q3),
    .Q2(reg4_1_q2), .Q1(reg4_1_q1), .Q0(reg4_1_q0));
  D_latch d_latch_1 (.R(\D锁存器演示 ), .WE(in_7), .D(d_latch_1_not_q), .Q(out_16), .not_Q(d_latch_1_not_q));
  seg7sel seg7sel_4 (
    .D3(reg4_1_q3), .D2(reg4_1_q2), .D1(reg4_1_q1), .D0(reg4_1_q0), .is_hex(1'b1), .a(seg7sel_4_a),
    .out_7(seg7sel_4_out_7), .out_8(seg7sel_4_out_8), .out_9(seg7sel_4_out_9), .out_10(seg7sel_4_out_10),
    .out_11(seg7sel_4_out_11), .out_12(seg7sel_4_out_12), .h(seg7sel_4_h));
  seg7sel seg7sel_5 (
    .D3(suber4_1_d3), .D2(suber4_1_d2), .D1(suber4_1_d1), .D0(suber4_1_d0), .is_hex(1'b1), .a(seg7sel_5_a),
    .out_7(seg7sel_5_out_7), .out_8(seg7sel_5_out_8), .out_9(seg7sel_5_out_9), .out_10(seg7sel_5_out_10),
    .out_11(seg7sel_5_out_11), .out_12(seg7sel_5_out_12), .h(seg7sel_5_h));
  _7_Segment_Display u_7_segment_display_5 (
    .g(seg7sel_5_out_12), .f(seg7sel_5_out_11), .a(seg7sel_5_a), .b(seg7sel_5_out_7), .e(seg7sel_5_out_10),
    .d(seg7sel_5_out_9), .c(seg7sel_5_out_8), .dp(seg7sel_5_h));
  _7_Segment_Display u_7_segment_display_6 (
    .g(seg7sel_4_out_12), .f(seg7sel_4_out_11), .a(seg7sel_4_a), .b(seg7sel_4_out_7), .e(seg7sel_4_out_10),
    .d(seg7sel_4_out_9), .c(seg7sel_4_out_8), .dp(seg7sel_4_h));

  // Notes on the sheet:
  //   说明
  //   这是f3和f5阶段搭建的所有电路，f3部分有些演示在main部分，
  //   f5阶段请转到sCPU部分查看
  //   比较器：演示
  //   4位原码加法器演示
  //   16进制4位加法器演示
  //   相比锁存器，D触发器没有震荡。
  //   因为后端信号写第一步时，无法写第二步。
  //   4位寄存器演示
  //   分析原因：在0和1之间来回变化
endmodule

module dcd (
  input  s1,
  input  s0,
  output r0,
  output r1,
  output r2,
  output r3
);

  wire not_1_out, not_2_out;

  not not_1 (not_1_out, s1);
  not not_2 (not_2_out, s0);
  nor nor_1 (r0, s1, s0);
  nor nor_2 (r1, s1, not_2_out);
  nor nor_3 (r2, not_1_out, s0);
  nor nor_4 (r3, not_1_out, not_2_out);
endmodule

module dcd3 (
  input  in_1,
  input  in_2,
  input  in_3,
  output out_4,
  output out_5,
  output out_6,
  output out_7,
  output out_8,
  output out_9,
  output out_10,
  output out_11
);

  wire and_1_out, and_2_out, dcd_1_r0, dcd_2_r0, nor_1_out, nor_2_out, not_1_out;

  nor nor_1 (nor_1_out, in_1, in_2);
  nor nor_2 (nor_2_out, in_1, in_3);
  and and_1 (and_1_out, in_1, in_2);
  and and_2 (and_2_out, in_1, in_3);
  dcd dcd_1 (.s1(nor_1_out), .s0(nor_2_out), .r0(dcd_1_r0), .r1(out_6), .r2(out_5), .r3(out_4));
  dcd dcd_2 (.s1(and_1_out), .s0(and_2_out), .r0(dcd_2_r0), .r1(out_9), .r2(out_10), .r3(out_11));
  not not_1 (not_1_out, in_1);
  and and_3 (out_8, in_1, dcd_2_r0);
  and and_4 (out_7, dcd_1_r0, not_1_out);
endmodule

module dec_dcd (
  input  in_1,
  input  in_2,
  input  in_3,
  input  in_4,
  output out_5,
  output b,
  output out_7,
  output d,
  output out_9,
  output f,
  output g,
  output h
);

  wire and_2_out, and_3_out, and_4_out, and_5_out, and_7_out, nand_1_out, nand_2_out, nand_3_out, nand_4_out,
       nor_1_out, nor_2_out, nor_3_out, not_1_out, not_2_out, not_3_out, not_4_out, or_1_out, or_2_out,
       or_3_out, or_4_out, or_5_out, xor_1_out, xor_2_out;

  and and_1 (h, in_1, or_1_out);
  or or_1 (or_1_out, in_2, in_3);
  not not_1 (not_1_out, in_3);
  nor nor_1 (nor_1_out, in_3, in_1);
  or or_2 (or_2_out, in_1, in_2);
  not not_2 (not_2_out, h);
  or or_3 (or_3_out, not_1_out, in_4);
  xor xor_1 (xor_1_out, in_4, in_2);
  not not_3 (not_3_out, or_2_out);
  or or_4 (or_4_out, or_2_out, or_3_out);
  and and_2 (and_2_out, not_3_out, and_3_out);
  and and_3 (and_3_out, not_1_out, in_4);
  nand nand_1 (nand_1_out, xor_1_out, nor_1_out);
  nand nand_2 (nand_2_out, and_4_out, in_2);
  not not_4 (not_4_out, in_4);
  nor nor_2 (nor_2_out, and_2_out, and_4_out);
  and and_4 (and_4_out, in_3, in_4);
  and and_5 (and_5_out, nand_1_out, nand_2_out);
  and and_6 (out_9, out_5, not_4_out);
  and and_7 (and_7_out, or_4_out, nor_2_out);
  nand nand_3 (nand_3_out, not_3_out, nor_3_out);
  xor xor_2 (xor_2_out, in_3, in_4);
  nand nand_4 (nand_4_out, in_2, xor_2_out);
  or or_5 (or_5_out, f, d);
  and and_8 (g, or_5_out, nand_3_out);
  nor nor_3 (nor_3_out, in_3, in_4);
  and and_9 (out_5, nand_1_out, not_2_out);
  and and_10 (b, nand_4_out, not_2_out);
  and and_11 (out_7, or_4_out, not_2_out);
  and and_12 (d, and_5_out, not_2_out);
  and and_13 (f, and_7_out, not_2_out);

  // Notes on the sheet:
  //   非0
  //   a
  //   c
  //   e
endmodule

module dcd4 (
  input  in_1,
  input  in_2,
  input  in_3,
  input  in_4,
  output out_5,
  output out_6,
  output out_7,
  output out_8,
  output out_9,
  output out_10,
  output out_11,
  output out_12,
  output out_13,
  output out_14,
  output out_15,
  output out_16,
  output out_17,
  output out_18,
  output out_19,
  output out_20
);

  wire and_1_out, and_2_out, and_3_out, dcd3_1_out_4, dcd3_2_out_4, nor_1_out, nor_2_out, nor_3_out,
       not_1_out;

  nor nor_1 (nor_1_out, in_1, in_2);
  nor nor_2 (nor_2_out, in_1, in_3);
  nor nor_3 (nor_3_out, in_1, in_4);
  and and_1 (and_1_out, in_1, in_2);
  and and_2 (and_2_out, in_1, in_3);
  and and_3 (and_3_out, in_1, in_4);
  dcd3 dcd3_1 (
    .in_1(nor_1_out), .in_2(nor_2_out), .in_3(nor_3_out), .out_4(dcd3_1_out_4), .out_5(out_11),
    .out_6(out_10), .out_7(out_9), .out_8(out_8), .out_9(out_7), .out_10(out_6), .out_11(out_5));
  dcd3 dcd3_2 (
    .in_1(and_1_out), .in_2(and_2_out), .in_3(and_3_out), .out_4(dcd3_2_out_4), .out_5(out_14),
    .out_6(out_15), .out_7(out_16), .out_8(out_17), .out_9(out_18), .out_10(out_19), .out_11(out_20));
  not not_1 (not_1_out, in_1);
  and and_4 (out_12, not_1_out, dcd3_1_out_4);
  and and_5 (out_13, in_1, dcd3_2_out_4);
endmodule

module hex (
  input  _3,
  input  _2,
  input  _1,
  input  _0,
  input  in_5,
  output a,
  output b,
  output c,
  output d,
  output e,
  output f,
  output g,
  output h
);

  wire and_2_out, and_3_out, dcd4_1_out_5, dcd4_1_out_6, dcd4_1_out_7, dcd4_1_out_8, dcd4_1_out_9,
       dcd4_1_out_10, dcd4_1_out_11, dcd4_1_out_12, dcd4_1_out_13, dcd4_1_out_14, dcd4_1_out_15,
       dcd4_1_out_16, dcd4_1_out_17, dcd4_1_out_18, dcd4_1_out_19, dcd4_1_out_20, not_1_out, not_2_out,
       not_3_out, or_1_out, or_2_out, or_3_out, or_4_out, or_5_out, or_6_out, or_7_out, or_8_1_out_9,
       or_8_2_out_9, or_8_out, or_9_out, or_10_out, or_12_out, or_13_out, or_15_out, or_19_out;

  dcd4 dcd4_1 (
    .in_1(_3), .in_2(_2), .in_3(_1), .in_4(_0), .out_5(dcd4_1_out_5), .out_6(dcd4_1_out_6),
    .out_7(dcd4_1_out_7), .out_8(dcd4_1_out_8), .out_9(dcd4_1_out_9), .out_10(dcd4_1_out_10),
    .out_11(dcd4_1_out_11), .out_12(dcd4_1_out_12), .out_13(dcd4_1_out_13), .out_14(dcd4_1_out_14),
    .out_15(dcd4_1_out_15), .out_16(dcd4_1_out_16), .out_17(dcd4_1_out_17), .out_18(dcd4_1_out_18),
    .out_19(dcd4_1_out_19), .out_20(dcd4_1_out_20));
  or or_1 (or_1_out, dcd4_1_out_5, dcd4_1_out_17);
  or or_2 (or_2_out, dcd4_1_out_12, dcd4_1_out_20);
  or or_3 (or_3_out, dcd4_1_out_8, dcd4_1_out_7);
  or or_4 (or_4_out, dcd4_1_out_10, dcd4_1_out_11);
  or or_5 (or_5_out, dcd4_1_out_16, dcd4_1_out_18);
  or or_6 (or_6_out, or_2_out, dcd4_1_out_15);
  not not_1 (not_1_out, or_6_out);
  not not_2 (not_2_out, _0);
  or or_7 (or_7_out, or_3_out, dcd4_1_out_18);
  not not_3 (not_3_out, or_7_out);
  or or_8 (or_8_out, or_4_out, dcd4_1_out_16);
  or or_9 (or_9_out, or_5_out, dcd4_1_out_20);
  OR_8 or_8_1 (
    .in_1(dcd4_1_out_5), .in_2(dcd4_1_out_6), .in_3(dcd4_1_out_8), .in_4(dcd4_1_out_9), .in_5(dcd4_1_out_12),
    .in_6(dcd4_1_out_13), .in_7(dcd4_1_out_14), .in_8(dcd4_1_out_15), .out_9(or_8_1_out_9));
  or or_10 (or_10_out, dcd4_1_out_9, or_5_out);
  OR_8 or_8_2 (
    .in_1(dcd4_1_out_7), .in_2(dcd4_1_out_8), .in_3(dcd4_1_out_10), .in_4(dcd4_1_out_11),
    .in_5(dcd4_1_out_13), .in_6(dcd4_1_out_14), .in_7(dcd4_1_out_15), .in_8(dcd4_1_out_19),
    .out_9(or_8_2_out_9));
  or or_11 (e, or_9_out, and_3_out);
  or or_12 (or_12_out, dcd4_1_out_18, or_8_1_out_9);
  or or_13 (or_13_out, or_1_out, dcd4_1_out_12);
  or or_14 (c, or_12_out, or_8_out);
  or or_15 (or_15_out, or_8_2_out_9, dcd4_1_out_20);
  or or_16 (b, dcd4_1_out_7, or_12_out);
  or or_17 (a, or_13_out, or_15_out);
  or or_18 (g, or_10_out, or_15_out);
  and and_1 (d, not_1_out, or_19_out);
  and and_2 (and_2_out, g, not_3_out);
  or or_19 (or_19_out, a, or_5_out);
  and and_3 (and_3_out, a, not_2_out);
  or or_20 (f, or_1_out, and_2_out);

  assign h = in_5;

  // Notes on the sheet:
  //   0表示低位，3表示高位
  //   此端口默认置0
  //   completed
  //   a-h表示7段数码管需要接的接口
endmodule

module OR_8 (
  input  in_1,
  input  in_2,
  input  in_3,
  input  in_4,
  input  in_5,
  input  in_6,
  input  in_7,
  input  in_8,
  output out_9
);

  wire nand_1_out, nand_2_out, nor_1_out, nor_2_out, nor_3_out, nor_4_out;

  nor nor_1 (nor_1_out, in_1, in_2);
  nor nor_2 (nor_2_out, in_3, in_4);
  nor nor_3 (nor_3_out, in_5, in_6);
  nor nor_4 (nor_4_out, in_7, in_8);
  nand nand_1 (nand_1_out, nor_1_out, nor_2_out);
  or or_1 (out_9, nand_1_out, nand_2_out);
  nand nand_2 (nand_2_out, nor_3_out, nor_4_out);
endmodule

module xor_v1 (
  input  in_1,
  input  in_2,
  output out_3
);

  wire and_1_out, nor_1_out;

  and and_1 (and_1_out, in_1, in_2);
  nor nor_1 (nor_1_out, in_1, in_2);
  nor nor_2 (out_3, and_1_out, nor_1_out);
endmodule

module tonghuo (
  input  in_1,
  input  in_2,
  output out_3
);

  wire not_1_out;

  not not_1 (not_1_out, in_2);
  Transistor transistor_1 (.in(not_1_out), .out(out_3), .gate(in_1));
  Transistor #(.\type ("n")) transistor_2 (.in(in_2), .out(out_3), .gate(in_1));
  Transistor transistor_3 (.in(in_1), .out(out_3), .gate(not_1_out));
  Transistor #(.\type ("n")) transistor_4 (.in(in_1), .out(out_3), .gate(in_2));
endmodule

module pri_enc_4_2 (
  input  is_0,
  input  is_1,
  input  is_2,
  input  is_3,
  output \信号有无 ,
  output \低位 ,
  output \高位 
);

  wire and_1_out, not_1_out, or_1_out;

  not not_1 (not_1_out, is_2);
  and and_1 (and_1_out, is_1, not_1_out);
  or or_1 (or_1_out, is_2, is_0);
  or or_2 (\低位 , and_1_out, is_3);
  or or_3 (\高位 , is_2, is_3);
  or or_4 (\信号有无 , or_1_out, \低位 );

  // Notes on the sheet:
  //   0
  //   1
  //   2
  //   3
endmodule

module pri_enc_16_4 (
  input  _0,
  input  in_2,
  input  in_3,
  input  in_4,
  input  in_5,
  input  in_6,
  input  in_7,
  input  in_8,
  input  in_9,
  input  in_10,
  input  in_11,
  input  in_12,
  input  in_13,
  input  in_14,
  input  in_15,
  input  _15,
  output out_17,
  output out_18,
  output out_19,
  output _3
);

  wire and_1_out, and_2_out, and_3_out, and_4_out, and_5_out, and_6_out, and_7_out, and_8_out, and_9_out,
       and_10_out, and_11_out, and_12_out, not_1_out, not_2_out, not_3_out, \pri_enc_4_2_1_低位 ,
       \pri_enc_4_2_1_信号有无 , \pri_enc_4_2_1_高位 , \pri_enc_4_2_2_低位 , \pri_enc_4_2_2_信号有无 ,
       \pri_enc_4_2_2_高位 , \pri_enc_4_2_3_低位 , \pri_enc_4_2_3_信号有无 , \pri_enc_4_2_3_高位 , \pri_enc_4_2_4_低位 ,
       \pri_enc_4_2_4_信号有无 , \pri_enc_4_2_4_高位 ;

  pri_enc_4_2 pri_enc_4_2_1 (
    .is_0(_0), .is_1(in_2), .is_2(in_3), .is_3(in_4), .\信号有无 (\pri_enc_4_2_1_信号有无 ),
    .\低位 (\pri_enc_4_2_1_低位 ), .\高位 (\pri_enc_4_2_1_高位 ));
  not not_1 (not_1_out, \pri_enc_4_2_2_信号有无 );
  pri_enc_4_2 pri_enc_4_2_2 (
    .is_0(in_5), .is_1(in_6), .is_2(in_7), .is_3(in_8), .\信号有无 (\pri_enc_4_2_2_信号有无 ),
    .\低位 (\pri_enc_4_2_2_低位 ), .\高位 (\pri_enc_4_2_2_高位 ));
  pri_enc_4_2 pri_enc_4_2_3 (
    .is_0(in_9), .is_1(in_10), .is_2(in_11), .is_3(in_12), .\信号有无 (\pri_enc_4_2_3_信号有无 ),
    .\低位 (\pri_enc_4_2_3_低位 ), .\高位 (\pri_enc_4_2_3_高位 ));
  not not_2 (not_2_out, \pri_enc_4_2_4_信号有无 );
  pri_enc_4_2 pri_enc_4_2_4 (
    .is_0(in_13), .is_1(in_14), .is_2(in_15), .is_3(_15), .\信号有无 (\pri_enc_4_2_4_信号有无 ),
    .\低位 (\pri_enc_4_2_4_低位 ), .\高位 (\pri_enc_4_2_4_高位 ));
  not not_3 (not_3_out, \pri_enc_4_2_3_信号有无 );
  and and_1 (and_1_out, not_1_out, and_5_out);
  and and_2 (and_2_out, not_3_out, and_4_out);
  and and_3 (and_3_out, \pri_enc_4_2_3_高位 , not_2_out);
  and and_4 (and_4_out, \pri_enc_4_2_2_高位 , not_2_out);
  and and_5 (and_5_out, not_3_out, and_7_out);
  and and_6 (and_6_out, not_1_out, and_11_out);
  and and_7 (and_7_out, \pri_enc_4_2_1_高位 , not_2_out);
  and and_8 (and_8_out, not_3_out, and_10_out);
  and and_9 (and_9_out, \pri_enc_4_2_3_低位 , not_2_out);
  and and_10 (and_10_out, \pri_enc_4_2_2_低位 , not_2_out);
  pri_enc_4_2 pri_enc_4_2_5 (
    .is_0(\pri_enc_4_2_1_信号有无 ), .is_1(\pri_enc_4_2_2_信号有无 ), .is_2(\pri_enc_4_2_3_信号有无 ),
    .is_3(\pri_enc_4_2_4_信号有无 ), .\低位 (out_19), .\高位 (_3));  // open: 信号有无
  and and_11 (and_11_out, not_3_out, and_12_out);
  and and_12 (and_12_out, \pri_enc_4_2_1_低位 , not_2_out);
  pri_enc_4_2 pri_enc_4_2_6 (
    .is_0(and_6_out), .is_1(and_8_out), .is_2(and_9_out), .is_3(\pri_enc_4_2_4_低位 ), .\信号有无 (out_17));  // open: 低位, 高位
  pri_enc_4_2 pri_enc_4_2_7 (
    .is_0(and_1_out), .is_1(and_2_out), .is_2(and_3_out), .is_3(\pri_enc_4_2_4_高位 ), .\信号有无 (out_18));  // open: 低位, 高位

  // Notes on the sheet:
  //   利用该电路，可以实现前导0的计数，即将16位数据从下到上输入电路，再对输出的4位分别取反，从下到上读数据。
  //   前导1计数只需要把输入取反，尾随0计数只需要把输入顺序颠倒就行。尾随1同理。
  //   0
endmodule

module chooser_1_2 (
  input  S,
  input  D0,
  input  D1,
  output Y
);

  wire and_1_out, and_2_out, not_1_out;

  not not_1 (not_1_out, S);
  and and_1 (and_1_out, S, D1);
  and and_2 (and_2_out, D0, not_1_out);
  or or_1 (Y, and_2_out, and_1_out);
endmodule

module chooser_3_4 (
  input  SH,
  input  SL,
  input  [2:0] D00,
  input  [2:0] D01,
  input  [2:0] D10,
  input  [2:0] D11,
  output [2:0] Y
);

  wire [2:0] and_1_out, and_2_out, and_3_out, and_4_out, or_1_out, or_2_out;
  wire [2:2] dcd_1_r0, dcd_1_r1, dcd_1_r2, dcd_1_r3;

  dcd dcd_1 (.s1(SH), .s0(SL), .r0(dcd_1_r0[2]), .r1(dcd_1_r1[2]), .r2(dcd_1_r2[2]), .r3(dcd_1_r3[2]));
  assign and_1_out = D00 & {3{dcd_1_r0[2]}};  // AND_Gate and_1, 3 bits wide
  assign and_2_out = D01 & {3{dcd_1_r1[2]}};  // AND_Gate and_2, 3 bits wide
  assign and_3_out = {3{dcd_1_r2[2]}} & D10;  // AND_Gate and_3, 3 bits wide
  assign and_4_out = {3{dcd_1_r3[2]}} & D11;  // AND_Gate and_4, 3 bits wide
  assign or_1_out = and_3_out | and_4_out;  // OR_Gate or_1, 3 bits wide
  assign or_2_out = and_1_out | and_2_out;  // OR_Gate or_2, 3 bits wide
  assign Y = or_2_out | or_1_out;  // OR_Gate or_3, 3 bits wide
endmodule

module AND_3 (
  input  [2:0] in_1,
  input  [2:0] in_2,
  output [2:0] out_3
);

  and and_1 (out_3[0], in_1[0], in_2[0]);
  and and_2 (out_3[1], in_1[1], in_2[1]);
  and and_3 (out_3[2], in_1[2], in_2[2]);

  // Notes on the sheet:
  //   in1
  //   in2
endmodule

module OR_3 (
  input  [2:0] in_1,
  input  [2:0] in_2,
  output [2:0] out_3
);

  or or_1 (out_3[0], in_1[0], in_2[0]);
  or or_2 (out_3[1], in_1[1], in_2[1]);
  or or_3 (out_3[2], in_1[2], in_2[2]);

  // Notes on the sheet:
  //   in1
  //   in2
endmodule

module seg7sel (
  input  D3,
  input  D2,
  input  D1,
  input  D0,
  input  is_hex,
  output a,
  output out_7,
  output out_8,
  output out_9,
  output out_10,
  output out_11,
  output out_12,
  output h
);

  wire dec_dcd_1_h, hex_1_a, hex_1_b, hex_1_c, hex_1_d, hex_1_e, hex_1_f, hex_1_g, nand_1_out, not_1_out;

  not not_1 (not_1_out, is_hex);
  nand nand_1 (nand_1_out, dec_dcd_1_h, not_1_out);
  dec_dcd dec_dcd_1 (
    .in_1(D3), .in_2(D2), .in_3(D1), .in_4(D0), .h(dec_dcd_1_h));  // open: out_5, b, out_7, d, out_9, f, g
  and and_1 (a, hex_1_a, nand_1_out);
  hex hex_1 (
    ._3(D3), ._2(D2), ._1(D1), ._0(D0), .in_5(1'b0), .a(hex_1_a), .b(hex_1_b), .c(hex_1_c), .d(hex_1_d),
    .e(hex_1_e), .f(hex_1_f), .g(hex_1_g));  // open: h
  and and_2 (out_7, hex_1_b, nand_1_out);
  and and_3 (out_12, hex_1_g, nand_1_out);
  not not_2 (h, nand_1_out);
  and and_4 (out_8, hex_1_c, nand_1_out);
  and and_5 (out_9, hex_1_d, nand_1_out);
  and and_6 (out_11, hex_1_f, nand_1_out);
  and and_7 (out_10, hex_1_e, nand_1_out);
endmodule

module comparer_4 (
  input  a3,
  input  a2,
  input  a1,
  input  a0,
  input  b3,
  input  b2,
  input  b1,
  input  b0,
  output o
);

  wire and_1_out, and_2_out, tonghuo_1_out_3, tonghuo_2_out_3, tonghuo_3_out_3, tonghuo_4_out_3;

  tonghuo tonghuo_1 (.in_1(a3), .in_2(b3), .out_3(tonghuo_1_out_3));
  and and_1 (and_1_out, tonghuo_1_out_3, tonghuo_2_out_3);
  tonghuo tonghuo_2 (.in_1(a2), .in_2(b2), .out_3(tonghuo_2_out_3));
  tonghuo tonghuo_3 (.in_1(a1), .in_2(b1), .out_3(tonghuo_3_out_3));
  and and_2 (and_2_out, tonghuo_3_out_3, tonghuo_4_out_3);
  tonghuo tonghuo_4 (.in_1(a0), .in_2(b0), .out_3(tonghuo_4_out_3));
  and and_3 (o, and_1_out, and_2_out);

  // Notes on the sheet:
  //   输入1
  //   输入2
  //   输出
endmodule

module adder1 (
  input  A1,
  input  A2,
  input  CL,
  output CH,
  output S
);

  wire and_1_out, and_2_out, xor_1_out;

  and and_1 (and_1_out, A1, A2);
  xor xor_1 (xor_1_out, A1, A2);
  and and_2 (and_2_out, xor_1_out, CL);
  xor xor_2 (S, xor_1_out, CL);
  or or_1 (CH, and_2_out, and_1_out);

  // Notes on the sheet:
  //   加数1
  //   加数2
  //   低位进位
  //   本位进位
  //   本位得数
endmodule

module adder4 (
  input  a3,
  input  a2,
  input  a1,
  input  a0,
  input  b3,
  input  b2,
  input  b1,
  input  b0,
  input  carry,
  output C,
  output S3,
  output S2,
  output S1,
  output S0
);

  wire adder1_2_ch, adder1_3_ch, adder1_4_ch;

  adder1 adder1_1 (.A1(a3), .A2(b3), .CL(adder1_2_ch), .CH(C), .S(S3));
  adder1 adder1_2 (.A1(a2), .A2(b2), .CL(adder1_3_ch), .CH(adder1_2_ch), .S(S2));
  adder1 adder1_3 (.A1(a1), .A2(b1), .CL(adder1_4_ch), .CH(adder1_3_ch), .S(S1));
  adder1 adder1_4 (.A1(a0), .A2(b0), .CL(carry), .CH(adder1_4_ch), .S(S0));
endmodule

module suber1 (
  input  SD,
  input  SR,
  input  LL,
  output LH,
  output D
);

  wire and_1_out, nor_1_out, not_1_out, xor_1_out;

  and and_1 (and_1_out, LL, SR);
  xor xor_1 (xor_1_out, SR, LL);
  not not_1 (not_1_out, xor_1_out);
  or or_1 (LH, and_1_out, nor_1_out);
  nor nor_1 (nor_1_out, SD, not_1_out);
  xor xor_2 (D, SD, xor_1_out);
endmodule

module suber4 (
  input  SD3,
  input  SD2,
  input  SD1,
  input  SD0,
  input  SR3,
  input  SR2,
  input  SR1,
  input  SR0,
  input  LL,
  output LH,
  output D3,
  output D2,
  output D1,
  output D0
);

  wire suber1_2_lh, suber1_3_lh, suber1_4_lh;

  suber1 suber1_1 (.SD(SD3), .SR(SR3), .LL(suber1_2_lh), .LH(LH), .D(D3));
  suber1 suber1_2 (.SD(SD2), .SR(SR2), .LL(suber1_3_lh), .LH(suber1_2_lh), .D(D2));
  suber1 suber1_3 (.SD(SD1), .SR(SR1), .LL(suber1_4_lh), .LH(suber1_3_lh), .D(D1));
  suber1 suber1_4 (.SD(SD0), .SR(SR0), .LL(LL), .LH(suber1_4_lh), .D(D0));
endmodule

module add_sm4 (
  input  A13,
  input  A12,
  input  A11,
  input  A10,
  input  A23,
  input  A22,
  input  A21,
  input  A20,
  output SGN,
  output R3,
  output R2,
  output R1,
  output R0
);

  wire adder4_1_s3, suber4_1_d3, suber4_1_lh, xor_1_out, xor_2_out;
  wire [2:0] adder4_1_s0, suber4_1_d0, suber4_2_d0;

  xor xor_1 (xor_1_out, A13, A23);
  adder4 adder4_1 (
    .a3(1'b0), .a2(A12), .a1(A11), .a0(A10), .b3(1'b0), .b2(A22), .b1(A21), .b0(A20), .carry(1'b0),
    .S3(adder4_1_s3), .S2(adder4_1_s0[2]), .S1(adder4_1_s0[1]), .S0(adder4_1_s0[0]));  // open: C
  suber4 suber4_1 (
    .SD3(1'b0), .SD2(A12), .SD1(A11), .SD0(A10), .SR3(1'b0), .SR2(A22), .SR1(A21), .SR0(A20), .LL(1'b0),
    .LH(suber4_1_lh), .D3(suber4_1_d3), .D2(suber4_1_d0[2]), .D1(suber4_1_d0[1]), .D0(suber4_1_d0[0]));
  suber4 suber4_2 (
    .SD3(1'b0), .SD2(A22), .SD1(A21), .SD0(A20), .SR3(1'b0), .SR2(A12), .SR1(A11), .SR0(A10), .LL(1'b0),
    .D2(suber4_2_d0[2]), .D1(suber4_2_d0[1]), .D0(suber4_2_d0[0]));  // open: LH, D3
  xor xor_2 (xor_2_out, A13, suber4_1_lh);
  chooser_1_2 chooser_1_2_1 (.S(A13), .D0(xor_1_out), .D1(xor_2_out), .Y(SGN));
  chooser_1_2 chooser_1_2_2 (.S(adder4_1_s3), .D0(xor_1_out), .D1(1'b0), .Y(R3));
  chooser_3_4 chooser_3_4_1 (
    .SH(xor_1_out), .SL(suber4_1_d3), .D00(adder4_1_s0), .D01(adder4_1_s0), .D10(suber4_1_d0),
    .D11(suber4_2_d0), .Y({R2, R1, R0}));

  // Notes on the sheet:
  //   符号位
  //   D0a指示加法器结果；D1a指示减法器结果
endmodule

module ocp4_sm (
  input  A13,
  input  A12,
  input  A11,
  input  A10,
  input  A23,
  input  A22,
  input  A21,
  input  A20,
  output out_9,
  output R3,
  output R2,
  output R1,
  output R0
);

  wire add_sm4_1_r0, add_sm4_1_r1, add_sm4_1_r2, xor_1_out, xor_2_out, xor_3_out, xor_4_out, xor_5_out,
       xor_6_out;

  xor xor_1 (xor_1_out, A23, A22);
  xor xor_2 (xor_2_out, A23, A21);
  xor xor_3 (xor_3_out, A13, A12);
  xor xor_4 (xor_4_out, A13, A11);
  xor xor_5 (xor_5_out, A13, A10);
  xor xor_6 (xor_6_out, A23, A20);
  add_sm4 add_sm4_1 (
    .A13(A13), .A12(xor_3_out), .A11(xor_4_out), .A10(xor_5_out), .A23(A23), .A22(xor_1_out),
    .A21(xor_2_out), .A20(xor_6_out), .SGN(out_9), .R3(R3), .R2(add_sm4_1_r2), .R1(add_sm4_1_r1),
    .R0(add_sm4_1_r0));
  xor xor_7 (R2, R3, add_sm4_1_r2);
  xor xor_8 (R1, R3, add_sm4_1_r1);
  xor xor_9 (R0, R3, add_sm4_1_r0);
endmodule

module tc4_overflow (
  input  a3,
  input  a2,
  input  a1,
  input  a0,
  input  b3,
  input  b2,
  input  b1,
  input  b0,
  input  carry,
  output ofl,
  output s3,
  output s2,
  output s1,
  output s0
);

  wire xor_1_out, xor_2_out;

  xor xor_1 (xor_1_out, b3, s3);
  xor xor_2 (xor_2_out, a3, s3);
  adder4 adder4_1 (
    .a3(a3), .a2(a2), .a1(a1), .a0(a0), .b3(b3), .b2(b2), .b1(b1), .b0(b0), .carry(carry), .S3(s3), .S2(s2),
    .S1(s1), .S0(s0));  // open: C
  and and_1 (ofl, xor_1_out, xor_2_out);

  // Notes on the sheet:
  //   在此列出溢出判断的逻辑：有且仅有同符号相加，且最终结果和开始反号的是溢出
endmodule

module SR_latch (
  input  R,
  input  S,
  output Q,
  output not_Q
);

  nor nor_1 (Q, R, not_Q);
  nor nor_2 (not_Q, Q, S);

  // Notes on the sheet:
  //   S=0,R=0
  //   S=0,R=1
  //   S=1,R=0
  //   S=1,R=1
  //   \bar{S}\bar{R}锁存器的真值表
  //   两端输出为1
  //   S端为1
  //   R端为1
  //   交叉配对反相器
endmodule

module D_latch (
  input  R,
  input  WE,
  input  D,
  output Q,
  output not_Q
);

  wire and_1_out, and_2_out, chooser_1_2_1_y, chooser_1_2_2_y, not_1_out;

  not not_1 (not_1_out, D);
  and and_1 (and_1_out, not_1_out, WE);
  and and_2 (and_2_out, WE, D);
  chooser_1_2 chooser_1_2_1 (.S(R), .D0(and_1_out), .D1(1'b1), .Y(chooser_1_2_1_y));
  chooser_1_2 chooser_1_2_2 (.S(R), .D0(and_2_out), .D1(1'b0), .Y(chooser_1_2_2_y));
  SR_latch sr_latch_1 (.R(chooser_1_2_1_y), .S(chooser_1_2_2_y), .Q(Q), .not_Q(not_Q));

  // Notes on the sheet:
  //   行为：WE开时把D的值写入Q，关时不写入东西
endmodule

module D_trigger (
  input  R,
  input  clk,
  input  D,
  output Q,
  output not_Q
);

  wire d_latch_1_q, not_1_out;

  not not_1 (not_1_out, clk);
  D_latch d_latch_1 (.R(R), .WE(not_1_out), .D(D), .Q(d_latch_1_q));  // open: not_Q
  D_latch d_latch_2 (.R(R), .WE(clk), .D(d_latch_1_q), .Q(Q), .not_Q(not_Q));

  // Notes on the sheet:
  //   D触发器的功能：在时钟从0快要到1时把电平送到Q
endmodule

module D_trigger_enable (
  input  R,
  input  clk,
  input  EN,
  input  D,
  output Q,
  output not_Q
);

  wire chooser_1_2_1_y;

  D_trigger d_trigger_1 (.R(R), .clk(clk), .D(chooser_1_2_1_y), .Q(Q), .not_Q(not_Q));
  chooser_1_2 chooser_1_2_1 (.S(EN), .D0(Q), .D1(D), .Y(chooser_1_2_1_y));

  // Notes on the sheet:
  //   功能，如果EN==1，则是D触发器，否则不改变Q的值
endmodule

module reg4 (
  input  R,
  input  clk,
  input  EN,
  input  D3,
  input  D2,
  input  D1,
  input  D0,
  output Q3,
  output Q2,
  output Q1,
  output Q0
);

  D_trigger_enable d_trigger_enable_1 (.R(R), .clk(clk), .EN(EN), .D(D3), .Q(Q3));  // open: not_Q
  D_trigger_enable d_trigger_enable_2 (.R(R), .clk(clk), .EN(EN), .D(D2), .Q(Q2));  // open: not_Q
  D_trigger_enable d_trigger_enable_3 (.R(R), .clk(clk), .EN(EN), .D(D1), .Q(Q1));  // open: not_Q
  D_trigger_enable d_trigger_enable_4 (.R(R), .clk(clk), .EN(EN), .D(D0), .Q(Q0));  // open: not_Q

  // Notes on the sheet:
  //   R用于把输出位全部置零
  //   EN==1能读写否则不能读写
  //   D3，D2,D1,D0当clk从0变为1时送到Q
endmodule

module counter4 (
  input  R,
  input  clk,
  input  EN,
  output Q3,
  output Q2,
  output Q1,
  output Q0
);

  wire adder4_1_s0, adder4_1_s1, adder4_1_s2, adder4_1_s3;

  reg4 reg4_1 (
    .R(R), .clk(clk), .EN(EN), .D3(adder4_1_s3), .D2(adder4_1_s2), .D1(adder4_1_s1), .D0(adder4_1_s0),
    .Q3(Q3), .Q2(Q2), .Q1(Q1), .Q0(Q0));
  adder4 adder4_1 (
    .a3(Q3), .a2(Q2), .a1(Q1), .a0(Q0), .b3(1'b0), .b2(1'b0), .b1(1'b0), .b0(1'b1), .carry(1'b0),
    .S3(adder4_1_s3), .S2(adder4_1_s2), .S1(adder4_1_s1), .S0(adder4_1_s0));  // open: C
endmodule

module seq_sum (
  input  in_1,
  input  in_2,
  input  in_3
);

  wire [3:0] counter4_1_q0;
  wire [7:0] adder8_1_s, reg8_1_q0;

  reg8 reg8_1 (
    .R(in_1), .clk(in_2), .EN(in_3), .D7(adder8_1_s[7]), .D6(adder8_1_s[6]), .D5(adder8_1_s[5]),
    .D4(adder8_1_s[4]), .D3(adder8_1_s[3]), .D2(adder8_1_s[2]), .D1(adder8_1_s[1]), .D0(adder8_1_s[0]),
    .Q7(reg8_1_q0[7]), .Q6(reg8_1_q0[6]), .Q5(reg8_1_q0[5]), .Q4(reg8_1_q0[4]), .Q3(reg8_1_q0[3]),
    .Q2(reg8_1_q0[2]), .Q1(reg8_1_q0[1]), .Q0(reg8_1_q0[0]));
  counter4 counter4_1 (
    .R(in_1), .clk(in_2), .EN(in_3), .Q3(counter4_1_q0[3]), .Q2(counter4_1_q0[2]), .Q1(counter4_1_q0[1]),
    .Q0(counter4_1_q0[0]));
  adder8 adder8_1 (.a(reg8_1_q0), .b({4'b0000, counter4_1_q0}), .cbefore(1'b0), .s(adder8_1_s));  // open: cafter

  // Notes on the sheet:
  //   手动产生时钟信号，计算1-10的和
  //   使用方法，先把R拨到1复位再拨回0；
  //   把EN设为1，接着拨clk开关使之产生10次1
endmodule

module adder8 (
  input  [7:0] a,
  input  [7:0] b,
  input  cbefore,
  output cafter,
  output [7:0] s
);

  wire adder4_2_c;

  adder4 adder4_1 (
    .a3(a[7]), .a2(a[6]), .a1(a[5]), .a0(a[4]), .b3(b[7]), .b2(b[6]), .b1(b[5]), .b0(b[4]),
    .carry(adder4_2_c), .C(cafter), .S3(s[7]), .S2(s[6]), .S1(s[5]), .S0(s[4]));
  adder4 adder4_2 (
    .a3(a[3]), .a2(a[2]), .a1(a[1]), .a0(a[0]), .b3(b[3]), .b2(b[2]), .b1(b[1]), .b0(b[0]), .carry(cbefore),
    .C(adder4_2_c), .S3(s[3]), .S2(s[2]), .S1(s[1]), .S0(s[0]));
endmodule

module reg8 (
  input  R,
  input  clk,
  input  EN,
  input  D7,
  input  D6,
  input  D5,
  input  D4,
  input  D3,
  input  D2,
  input  D1,
  input  D0,
  output Q7,
  output Q6,
  output Q5,
  output Q4,
  output Q3,
  output Q2,
  output Q1,
  output Q0
);

  reg4 reg4_1 (.R(R), .clk(clk), .EN(EN), .D3(D7), .D2(D6), .D1(D5), .D0(D4), .Q3(Q7), .Q2(Q6), .Q1(Q5), .Q0(Q4));
  reg4 reg4_2 (.R(R), .clk(clk), .EN(EN), .D3(D3), .D2(D2), .D1(D1), .D0(D0), .Q3(Q3), .Q2(Q2), .Q1(Q1), .Q0(Q0));
endmodule

module electronic_clock (
  input  R,
  input  EN
);

  wire and_1_out, and_2_out, and_3_out, and_4_out, clk_out, counter4_1_q0, counter4_1_q1, counter4_1_q2,
       counter4_1_q3, counter4_2_q0, counter4_2_q1, counter4_2_q2, counter4_2_q3, counter4_3_q0,
       counter4_3_q1, counter4_3_q2, counter4_3_q3, counter4_4_q0, counter4_4_q1, counter4_4_q2,
       counter4_4_q3, or_1_out, or_2_out, or_3_out, or_4_out, seg7sel_1_a, seg7sel_1_h, seg7sel_1_out_7,
       seg7sel_1_out_8, seg7sel_1_out_9, seg7sel_1_out_10, seg7sel_1_out_11, seg7sel_1_out_12, seg7sel_2_a,
       seg7sel_2_h, seg7sel_2_out_7, seg7sel_2_out_8, seg7sel_2_out_9, seg7sel_2_out_10, seg7sel_2_out_11,
       seg7sel_2_out_12, seg7sel_3_a, seg7sel_3_h, seg7sel_3_out_7, seg7sel_3_out_8, seg7sel_3_out_9,
       seg7sel_3_out_10, seg7sel_3_out_11, seg7sel_3_out_12, seg7sel_4_a, seg7sel_4_h, seg7sel_4_out_7,
       seg7sel_4_out_8, seg7sel_4_out_9, seg7sel_4_out_10, seg7sel_4_out_11, seg7sel_4_out_12;

  Clock clk (.out(clk_out));
  or or_1 (or_1_out, and_1_out, R);
  or or_2 (or_2_out, and_2_out, R);
  or or_3 (or_3_out, and_3_out, R);
  or or_4 (or_4_out, and_4_out, R);
  counter4 counter4_1 (
    .R(or_1_out), .clk(and_2_out), .EN(EN), .Q3(counter4_1_q3), .Q2(counter4_1_q2), .Q1(counter4_1_q1),
    .Q0(counter4_1_q0));
  counter4 counter4_2 (
    .R(or_2_out), .clk(and_3_out), .EN(EN), .Q3(counter4_2_q3), .Q2(counter4_2_q2), .Q1(counter4_2_q1),
    .Q0(counter4_2_q0));
  counter4 counter4_3 (
    .R(or_3_out), .clk(and_4_out), .EN(EN), .Q3(counter4_3_q3), .Q2(counter4_3_q2), .Q1(counter4_3_q1),
    .Q0(counter4_3_q0));
  counter4 counter4_4 (
    .R(or_4_out), .clk(clk_out), .EN(EN), .Q3(counter4_4_q3), .Q2(counter4_4_q2), .Q1(counter4_4_q1),
    .Q0(counter4_4_q0));
  and and_1 (and_1_out, counter4_1_q2, counter4_1_q1);
  and and_2 (and_2_out, counter4_2_q3, counter4_2_q1);
  and and_3 (and_3_out, counter4_3_q2, counter4_3_q1);
  and and_4 (and_4_out, counter4_4_q3, counter4_4_q1);
  seg7sel seg7sel_1 (
    .D3(counter4_1_q3), .D2(counter4_1_q2), .D1(counter4_1_q1), .D0(counter4_1_q0), .is_hex(1'b1),
    .a(seg7sel_1_a), .out_7(seg7sel_1_out_7), .out_8(seg7sel_1_out_8), .out_9(seg7sel_1_out_9),
    .out_10(seg7sel_1_out_10), .out_11(seg7sel_1_out_11), .out_12(seg7sel_1_out_12), .h(seg7sel_1_h));
  _7_Segment_Display u_7_segment_display_1 (
    .g(seg7sel_1_out_12), .f(seg7sel_1_out_11), .a(seg7sel_1_a), .b(seg7sel_1_out_7), .e(seg7sel_1_out_10),
    .d(seg7sel_1_out_9), .c(seg7sel_1_out_8), .dp(seg7sel_1_h));
  seg7sel seg7sel_2 (
    .D3(counter4_2_q3), .D2(counter4_2_q2), .D1(counter4_2_q1), .D0(counter4_2_q0), .is_hex(1'b1),
    .a(seg7sel_2_a), .out_7(seg7sel_2_out_7), .out_8(seg7sel_2_out_8), .out_9(seg7sel_2_out_9),
    .out_10(seg7sel_2_out_10), .out_11(seg7sel_2_out_11), .out_12(seg7sel_2_out_12), .h(seg7sel_2_h));
  seg7sel seg7sel_3 (
    .D3(counter4_3_q3), .D2(counter4_3_q2), .D1(counter4_3_q1), .D0(counter4_3_q0), .is_hex(1'b1),
    .a(seg7sel_3_a), .out_7(seg7sel_3_out_7), .out_8(seg7sel_3_out_8), .out_9(seg7sel_3_out_9),
    .out_10(seg7sel_3_out_10), .out_11(seg7sel_3_out_11), .out_12(seg7sel_3_out_12), .h(seg7sel_3_h));
  seg7sel seg7sel_4 (
    .D3(counter4_4_q3), .D2(counter4_4_q2), .D1(counter4_4_q1), .D0(counter4_4_q0), .is_hex(1'b1),
    .a(seg7sel_4_a), .out_7(seg7sel_4_out_7), .out_8(seg7sel_4_out_8), .out_9(seg7sel_4_out_9),
    .out_10(seg7sel_4_out_10), .out_11(seg7sel_4_out_11), .out_12(seg7sel_4_out_12), .h(seg7sel_4_h));
  _7_Segment_Display u_7_segment_display_2 (
    .g(seg7sel_2_out_12), .f(seg7sel_2_out_11), .a(seg7sel_2_a), .b(seg7sel_2_out_7), .e(seg7sel_2_out_10),
    .d(seg7sel_2_out_9), .c(seg7sel_2_out_8), .dp(seg7sel_2_h));
  _7_Segment_Display u_7_segment_display_3 (
    .g(seg7sel_3_out_12), .f(seg7sel_3_out_11), .a(seg7sel_3_a), .b(seg7sel_3_out_7), .e(seg7sel_3_out_10),
    .d(seg7sel_3_out_9), .c(seg7sel_3_out_8), .dp(seg7sel_3_h));
  _7_Segment_Display u_7_segment_display_4 (
    .g(seg7sel_4_out_12), .f(seg7sel_4_out_11), .a(seg7sel_4_a), .b(seg7sel_4_out_7), .e(seg7sel_4_out_10),
    .d(seg7sel_4_out_9), .c(seg7sel_4_out_8), .dp(seg7sel_4_h));
endmodule

module xor_v0 (
  input  in_1,
  input  in_2,
  output out_3
);

  wire transistor_3_out, transistor_5_out;

  Transistor #(.\type ("n")) transistor_1 (.in(transistor_5_out), .out(out_3), .gate(in_1));
  Transistor transistor_2 (.in(transistor_3_out), .out(out_3), .gate(in_1));
  Transistor transistor_3 (.in(1'b0), .out(transistor_3_out), .gate(in_2));
  Transistor #(.\type ("n")) transistor_4 (.in(1'b1), .out(transistor_3_out), .gate(in_2));
  Transistor transistor_5 (.in(1'b1), .out(transistor_5_out), .gate(in_2));
  Transistor #(.\type ("n")) transistor_6 (.in(1'b0), .out(transistor_5_out), .gate(in_2));
endmodule

module mux_8_2 (
  input  S,
  input  [7:0] D0,
  input  [7:0] D1,
  output [7:0] Y
);

  wire [7:0] and_1_out, and_2_out, not_1_out;

  assign and_1_out = D0 & not_1_out;  // AND_Gate and_1, 8 bits wide
  assign not_1_out = ~{8{S}};  // NOT_Gate not_1, 8 bits wide
  assign and_2_out = {8{S}} & D1;  // AND_Gate and_2, 8 bits wide
  assign Y = and_1_out | and_2_out;  // OR_Gate or_1, 8 bits wide
endmodule

module mux_8_16 (
  input  [3:0] S,
  input  [7:0] R0,
  input  [7:0] R1,
  input  [7:0] R2,
  input  [7:0] R3,
  input  [7:0] R4,
  input  [7:0] R5,
  input  [7:0] R6,
  input  [7:0] R7,
  input  [7:0] R8,
  input  [7:0] R9,
  input  [7:0] RA,
  input  [7:0] RB,
  input  [7:0] RC,
  input  [7:0] RD,
  input  [7:0] RE,
  input  [7:0] RF,
  output [7:0] selected
);

  wire [7:0] mux_8_2_1_y, mux_8_2_2_y, mux_8_2_3_y, mux_8_2_4_y, mux_8_2_5_y, mux_8_2_6_y, mux_8_2_7_y,
       mux_8_2_8_y, mux_8_2_9_y, mux_8_2_10_y, mux_8_2_11_y, mux_8_2_12_y, mux_8_2_13_y, mux_8_2_14_y;

  mux_8_2 mux_8_2_1 (.S(S[0]), .D0(R0), .D1(R1), .Y(mux_8_2_1_y));
  mux_8_2 mux_8_2_2 (.S(S[0]), .D0(R2), .D1(R3), .Y(mux_8_2_2_y));
  mux_8_2 mux_8_2_3 (.S(S[0]), .D0(R4), .D1(R5), .Y(mux_8_2_3_y));
  mux_8_2 mux_8_2_4 (.S(S[0]), .D0(R6), .D1(R7), .Y(mux_8_2_4_y));
  mux_8_2 mux_8_2_5 (.S(S[0]), .D0(R8), .D1(R9), .Y(mux_8_2_5_y));
  mux_8_2 mux_8_2_6 (.S(S[0]), .D0(RA), .D1(RB), .Y(mux_8_2_6_y));
  mux_8_2 mux_8_2_7 (.S(S[0]), .D0(RC), .D1(RD), .Y(mux_8_2_7_y));
  mux_8_2 mux_8_2_8 (.S(S[0]), .D0(RE), .D1(RF), .Y(mux_8_2_8_y));
  mux_8_2 mux_8_2_9 (.S(S[1]), .D0(mux_8_2_1_y), .D1(mux_8_2_2_y), .Y(mux_8_2_9_y));
  mux_8_2 mux_8_2_10 (.S(S[1]), .D0(mux_8_2_3_y), .D1(mux_8_2_4_y), .Y(mux_8_2_10_y));
  mux_8_2 mux_8_2_11 (.S(S[1]), .D0(mux_8_2_5_y), .D1(mux_8_2_6_y), .Y(mux_8_2_11_y));
  mux_8_2 mux_8_2_12 (.S(S[1]), .D0(mux_8_2_7_y), .D1(mux_8_2_8_y), .Y(mux_8_2_12_y));
  mux_8_2 mux_8_2_13 (.S(S[2]), .D0(mux_8_2_9_y), .D1(mux_8_2_10_y), .Y(mux_8_2_13_y));
  mux_8_2 mux_8_2_14 (.S(S[2]), .D0(mux_8_2_11_y), .D1(mux_8_2_12_y), .Y(mux_8_2_14_y));
  mux_8_2 mux_8_2_15 (.S(S[3]), .D0(mux_8_2_13_y), .D1(mux_8_2_14_y), .Y(selected));
endmodule

module sCPU (
  input  R,
  input  EN,
  output [3:0] out_3,
  output [7:0] out_4
);

  wire and_1_out, and_2_out, and_3_out, and_4_out, and_7_out, and_10_out, and_11_out, and_12_out,
       clock_1_out, er0, not_1_out, not_2_out, not_3_out, write_id_r0, write_id_r1, write_id_r2, write_id_r3;
  wire [1:0] high_2_bits;
  wire [3:0] adder_4_new_1_s, low_4_bits, mux_4_2_1_y, mux_4_4_1_y;
  wire [3:2] mid_4_bits;
  wire [7:0] add_operand_1_y, add_operand_2_y, adder8_1_s, and_8_out, and_9_out, bner0_operand_y,
       mux_8_4_1_y, r0_qs, r1_qs, r3_qs, register_output_y, seg7sel_1_h, seg7sel_2_h;
  wire [7:7] and_5_out, and_6_out;

  Clock clock_1 (.out(clock_1_out));
  mux_4_2 mux_4_2_1 (.S(er0), .D0({mid_4_bits, low_4_bits[3:2]}), .D1(adder_4_new_1_s), .Y(mux_4_2_1_y));
  and and_1 (and_1_out, and_10_out, EN);
  mux_8_4 register_output (
    .S(high_2_bits), .D0(adder8_1_s), .D2({4'b0000, low_4_bits}), .Y(register_output_y));  // open: D1, D3
  mux_4_4 mux_4_4_1 (
    .S(high_2_bits), .D0(adder_4_new_1_s), .D1(adder_4_new_1_s), .D2(adder_4_new_1_s), .D3(mux_4_2_1_y),
    .Y(mux_4_4_1_y));
  reg8_new r0 (.R(R), .clk(clock_1_out), .EN(and_1_out), .Ds(register_output_y), .Qs(r0_qs));
  and and_2 (and_2_out, and_12_out, EN);
  adder_4_new adder_4_new_1 (.a(4'b0001), .b(out_3), .c_before(1'b0), .s(adder_4_new_1_s));  // open: c_after
  reg4_new PC (.R(R), .clk(clock_1_out), .EN(EN), .D(mux_4_4_1_y), .Q(out_3));
  mux_8_4 add_operand_2 (.S(low_4_bits[1:0]), .D0(r0_qs), .D1(r1_qs), .D2(out_4), .D3(r3_qs), .Y(add_operand_2_y));
  mux_8_4 add_operand_1 (.S(low_4_bits[3:2]), .D0(r0_qs), .D1(r1_qs), .D2(out_4), .D3(r3_qs), .Y(add_operand_1_y));
  mux_8_4 mux_8_4_1 (.S(low_4_bits[1:0]), .D0(r0_qs), .D1(r1_qs), .D2(out_4), .D3(r3_qs), .Y(mux_8_4_1_y));
  reg8_new r1 (.R(R), .clk(clock_1_out), .EN(and_2_out), .Ds(register_output_y), .Qs(r1_qs));
  and and_3 (and_3_out, and_11_out, EN);
  adder8 adder8_1 (.a(add_operand_2_y), .b(add_operand_1_y), .cbefore(1'b0), .s(adder8_1_s));  // open: cafter
  mux_8_4 bner0_operand (.S(low_4_bits[1:0]), .D0(r0_qs), .D1(r1_qs), .D2(out_4), .D3(r3_qs), .Y(bner0_operand_y));
  seg7sel seg7sel_1 (
    .D3(mux_8_4_1_y[7]), .D2(mux_8_4_1_y[6]), .D1(mux_8_4_1_y[5]), .D0(mux_8_4_1_y[4]), .is_hex(1'b1),
    .a(seg7sel_1_h[7]), .out_7(seg7sel_1_h[6]), .out_8(seg7sel_1_h[5]), .out_9(seg7sel_1_h[4]),
    .out_10(seg7sel_1_h[3]), .out_11(seg7sel_1_h[2]), .out_12(seg7sel_1_h[1]), .h(seg7sel_1_h[0]));
  seg7sel seg7sel_2 (
    .D3(mux_8_4_1_y[3]), .D2(mux_8_4_1_y[2]), .D1(mux_8_4_1_y[1]), .D0(mux_8_4_1_y[0]), .is_hex(1'b1),
    .a(seg7sel_2_h[7]), .out_7(seg7sel_2_h[6]), .out_8(seg7sel_2_h[5]), .out_9(seg7sel_2_h[4]),
    .out_10(seg7sel_2_h[3]), .out_11(seg7sel_2_h[2]), .out_12(seg7sel_2_h[1]), .h(seg7sel_2_h[0]));
  mux_8_16 memory (
    .S(out_3), .R0(8'h8a), .R1(8'h90), .R2(8'ha0), .R3(8'hb1), .R4(8'h17), .R5(8'h29), .R6(8'hd1),
    .R7(8'he3), .R8(8'h42), .R9({8{1'b0}}), .RA({8{1'b0}}), .RB({8{1'b0}}), .RC({8{1'b0}}), .RD({8{1'b0}}),
    .RE({8{1'b0}}), .RF({8{1'b0}}), .selected({high_2_bits, mid_4_bits, low_4_bits}));
  reg8_new r2 (.R(R), .clk(clock_1_out), .EN(and_3_out), .Ds(register_output_y), .Qs(out_4));
  not not_1 (not_1_out, high_2_bits[0]);
  and and_4 (and_4_out, and_7_out, EN);
  and and_5 (and_5_out[7], high_2_bits[0], not_2_out);
  not not_2 (not_2_out, high_2_bits[1]);
  not not_3 (not_3_out, high_2_bits[1]);
  comparer_8 comparer_8_1 (.in_1(r0_qs), .in_2(bner0_operand_y), .out_3(er0));
  and and_6 (and_6_out[7], high_2_bits[0], not_3_out);
  dcd write_id (
    .s1(mid_4_bits[3]), .s0(mid_4_bits[2]), .r0(write_id_r0), .r1(write_id_r1), .r2(write_id_r2),
    .r3(write_id_r3));
  and and_7 (and_7_out, not_1_out, write_id_r3);
  reg8_new r3 (.R(R), .clk(clock_1_out), .EN(and_4_out), .Ds(register_output_y), .Qs(r3_qs));
  assign and_8_out = seg7sel_1_h & {8{and_5_out[7]}};  // AND_Gate and_8, 8 bits wide
  assign and_9_out = seg7sel_2_h & {8{and_6_out[7]}};  // AND_Gate and_9, 8 bits wide
  and and_10 (and_10_out, not_1_out, write_id_r0);
  and and_11 (and_11_out, not_1_out, write_id_r2);
  and and_12 (and_12_out, not_1_out, write_id_r1);
  _7_Segment_Display u_7_segment_display_1 (
    .g(and_8_out[1]), .f(and_8_out[2]), .a(and_8_out[7]), .b(and_8_out[6]), .e(and_8_out[3]),
    .d(and_8_out[4]), .c(and_8_out[5]), .dp(and_8_out[0]));
  _7_Segment_Display u_7_segment_display_2 (
    .g(and_9_out[1]), .f(and_9_out[2]), .a(and_9_out[7]), .b(and_9_out[6]), .e(and_9_out[3]),
    .d(and_9_out[4]), .c(and_9_out[5]), .dp(and_9_out[0]));

  // Other names for the same wires on the sheet: mid_4_bits[1:0] = low_4_bits[3:2]

  // Notes on the sheet:
  //   而能完成数列求和的sCPU元件更多，所以它更具通用性，能够通过修改程序调整参数，能完成的运算需求也更多
  //   out指令，编码为01，最后两位表示需显示的寄存器
  //   和数列求和专用电路seq_sum部分对比：
  //   seq_sum元件更少，因而占用空间少，更简单、容易调试；
  //   如果需要10以内奇数求和，则修改程序为8b 91 a0 b2 29 17 d1 df 00 00 00 00 00 00 00 00
  //   不能设计10个数相加的指令，否则指令位宽需要至少20位，同时寄存器要至少10个
  //   在这个指令集架构中，指令第二位为0的一定可以写入寄存器
  //   高位
  //   低位
endmodule

module reg4_new (
  input  R,
  input  clk,
  input  EN,
  input  [3:0] D,
  output [3:0] Q
);

  reg4 reg4_1 (
    .R(R), .clk(clk), .EN(EN), .D3(D[3]), .D2(D[2]), .D1(D[1]), .D0(D[0]), .Q3(Q[3]), .Q2(Q[2]), .Q1(Q[1]),
    .Q0(Q[0]));
endmodule

module reg8_new (
  input  R,
  input  clk,
  input  EN,
  input  [7:0] Ds,
  output [7:0] Qs
);

  reg4_new reg4_new_1 (.R(R), .clk(clk), .EN(EN), .D(Ds[7:4]), .Q(Qs[7:4]));
  reg4_new reg4_new_2 (.R(R), .clk(clk), .EN(EN), .D(Ds[3:0]), .Q(Qs[3:0]));
endmodule

module mux_8_4 (
  input  [1:0] S,
  input  [7:0] D0,
  input  [7:0] D1,
  input  [7:0] D2,
  input  [7:0] D3,
  output [7:0] Y
);

  wire [7:0] mux_8_2_1_y, mux_8_2_2_y;

  mux_8_2 mux_8_2_1 (.S(S[0]), .D0(D0), .D1(D1), .Y(mux_8_2_1_y));
  mux_8_2 mux_8_2_2 (.S(S[0]), .D0(D2), .D1(D3), .Y(mux_8_2_2_y));
  mux_8_2 mux_8_2_3 (.S(S[1]), .D0(mux_8_2_1_y), .D1(mux_8_2_2_y), .Y(Y));
endmodule

module comparer_8 (
  input  [7:0] in_1,
  input  [7:0] in_2,
  output out_3
);

  wire [1:0] or_2_out;
  wire [3:0] or_1_out;
  wire [7:0] xor_1_out;

  assign xor_1_out = in_1 ^ in_2;  // XOR_Gate xor_1, 8 bits wide
  assign or_1_out = xor_1_out[3:0] | xor_1_out[7:4];  // OR_Gate or_1, 4 bits wide
  assign or_2_out = or_1_out[1:0] | or_1_out[3:2];  // OR_Gate or_2, 2 bits wide
  nor nor_1 (out_3, or_2_out[0], or_2_out[1]);
endmodule

module adder_4_new (
  input  [3:0] a,
  input  [3:0] b,
  input  c_before,
  output c_after,
  output [3:0] s
);

  adder4 adder4_1 (
    .a3(a[3]), .a2(a[2]), .a1(a[1]), .a0(a[0]), .b3(b[3]), .b2(b[2]), .b1(b[1]), .b0(b[0]), .carry(c_before),
    .C(c_after), .S3(s[3]), .S2(s[2]), .S1(s[1]), .S0(s[0]));
endmodule

module mux_4_4 (
  input  [1:0] S,
  input  [3:0] D0,
  input  [3:0] D1,
  input  [3:0] D2,
  input  [3:0] D3,
  output [3:0] Y
);

  wire [3:0] mux_4_2_1_y, mux_4_2_2_y;

  mux_4_2 mux_4_2_1 (.S(S[0]), .D0(D0), .D1(D1), .Y(mux_4_2_1_y));
  mux_4_2 mux_4_2_2 (.S(S[0]), .D0(D2), .D1(D3), .Y(mux_4_2_2_y));
  mux_4_2 mux_4_2_3 (.S(S[1]), .D0(mux_4_2_1_y), .D1(mux_4_2_2_y), .Y(Y));
endmodule

module mux_4_2 (
  input  S,
  input  [3:0] D0,
  input  [3:0] D1,
  output [3:0] Y
);

  wire [3:0] and_1_out, and_2_out, not_1_out;

  assign and_1_out = D0 & not_1_out;  // AND_Gate and_1, 4 bits wide
  assign not_1_out = ~{4{S}};  // NOT_Gate not_1, 4 bits wide
  assign and_2_out = {4{S}} & D1;  // AND_Gate and_2, 4 bits wide
  assign Y = and_1_out | and_2_out;  // OR_Gate or_1, 4 bits wide
endmodule
