// Logisim project f6_minirv.circ as structural Verilog: 3 circuits, main circuit main
module main (
);


  // Notes on the sheet:
  //   rv32E只有16个寄存器
  //   PC寄存器的位宽：32位
  //   共有31个GPR
  //   sISA的r0可以随意赋值，而RV32I的r0的所有位为0不变
  //   指令编码位宽为32位，一共有R,I,S,U四种基本格式
  //   使用5位表达一个GPR，因为共有2^5=32个GPR
  //   add指令：0000000[rs2][rs1]000[rd]0110011
endmodule

module minirv (
  input  R,
  output [9:0] out_2,
  output [31:0] out_3,
  output [31:0] out_4,
  output [31:0] out_5,
  output [31:0] out_6
);

  wire and_1_out, and_2_out, and_10_out, clock_1_out, comparator_1_lt, comparator_3_eq, comparator_4_eq,
       comparator_5_eq, comparator_6_eq, comparator_7_eq, comparator_8_eq, comparator_9_eq, comparator_10_eq,
       comparator_11_eq, comparator_13_eq, does_read_memory, does_write_memory, GPR_WE, is_sb, isVGA;
  wire [3:0] decoder_1_out0, multiplexer_2_out;
  wire [6:0] high_7_bits;
  wire [7:0] multiplexer_5_out, xcoor, ycoor;
  wire [11:7] program_data;
  wire [24:15] lui_result;
  wire [31:0] add_result, addi_result, and_3_out, and_4_out, and_5_out, and_6_out, and_7_out, and_8_out,
       and_9_out, bit_extender_1_out, bit_extender_2_out, bit_extender_3_out, bit_extender_4_out,
       bit_extender_5_out, bit_extender_6_out, bit_extender_7_out, bit_extender_8_out, counter_1_q,
       GPRs_rs1_val, lbu_result, multiplexer_1_out, multiplexer_3_out, mwrite_addr, PC_read, rs2_val, wdata;

  Counter #(.max('hffffffff), .ongoal("stay"), .width(32)) counter_1 (
    .clr(R), .load(1'b0), .up(1'b1), .clk(and_1_out), .Q(counter_1_q));  // open: count, D, carry
  Clock clock_1 (.out(clock_1_out));
  and and_1 (and_1_out, clock_1_out, comparator_1_lt);
  Comparator #(.width(32)) comparator_1 (.a(counter_1_q), .b(32'h99520), .lt(comparator_1_lt));  // open: gt, eq
  Register #(.width(32)) register_1 (.D(out_4), .en(1'b1), .clk(and_1_out), .Q(PC_read), .clr(R));
  Comparator #(.width(10)) comparator_2 (.a(out_2), .b(10'h23), .eq(is_sb));  // open: gt, lt
  ROM #(.addrWidth(18), .dataWidth(32)) \program  (
    .addr(PC_read[19:2]), .data({high_7_bits, lui_result, out_2[9:7], program_data, out_2[6:0]}));
  Comparator #(.width(10)) comparator_3 (.a(out_2), .b(10'h103), .eq(comparator_3_eq));  // open: gt, lt
  Comparator #(.width(10)) comparator_4 (.a(out_2), .b(10'h203), .eq(comparator_4_eq));  // open: gt, lt
  Comparator #(.width(10)) comparator_5 (.a(out_2), .b(10'h123), .eq(comparator_5_eq));  // open: gt, lt
  assign bit_extender_1_out = {{31{comparator_6_eq}}, comparator_6_eq};  // Bit_Extender bit_extender_1
  Comparator #(.width(10)) comparator_6 (.a(out_2), .b(10'h67), .eq(comparator_6_eq));  // open: gt, lt
  or or_1 (does_write_memory, comparator_5_eq, is_sb);
  assign bit_extender_2_out = {{31{comparator_7_eq}}, comparator_7_eq};  // Bit_Extender bit_extender_2
  Comparator #(.width(10)) comparator_7 (.a(out_2), .b(10'h13), .eq(comparator_7_eq));  // open: gt, lt
  Comparator #(.width(10)) comparator_8 (.a(out_2), .b(10'h33), .eq(comparator_8_eq));  // open: gt, lt
  and and_2 (and_2_out, comparator_8_eq, comparator_9_eq);
  Comparator #(.width(7)) comparator_9 (.a(high_7_bits), .b({7{1'b0}}), .eq(comparator_9_eq));  // open: gt, lt
  assign bit_extender_3_out = {{31{comparator_10_eq}}, comparator_10_eq};  // Bit_Extender bit_extender_3
  Comparator #(.width(7)) comparator_10 (.a(out_2[6:0]), .b(7'b0110111), .eq(comparator_10_eq));  // open: gt, lt
  or or_2 (does_read_memory, comparator_4_eq, comparator_3_eq);
  assign and_3_out = bit_extender_2_out & addi_result;  // AND_Gate and_3, 32 bits wide
  assign bit_extender_4_out = {{31{and_2_out}}, and_2_out};  // Bit_Extender bit_extender_4
  assign and_4_out = bit_extender_3_out & {high_7_bits, lui_result, out_2[9:7], {12{1'b0}}};  // AND_Gate and_4, 32 bits wide
  assign bit_extender_5_out = {{20{high_7_bits[6]}}, {high_7_bits, lui_result[24:20]}};  // Bit_Extender bit_extender_5
  assign and_5_out = bit_extender_4_out & add_result;  // AND_Gate and_5, 32 bits wide
  assign and_6_out = out_3 & bit_extender_1_out;  // AND_Gate and_6, 32 bits wide
  assign bit_extender_6_out = {{31{comparator_4_eq}}, comparator_4_eq};  // Bit_Extender bit_extender_6
  assign bit_extender_7_out = {{20{high_7_bits[6]}}, {high_7_bits, program_data}};  // Bit_Extender bit_extender_7
  Adder #(.width(32)) adder_1 (.a(GPRs_rs1_val), .b(bit_extender_5_out), .out(addi_result));  // open: cin, cout
  assign bit_extender_8_out = {{31{comparator_3_eq}}, comparator_3_eq};  // Bit_Extender bit_extender_8
  assign and_7_out = bit_extender_6_out & lbu_result;  // AND_Gate and_7, 32 bits wide
  Decoder #(.select(2)) decoder_1 (
    .out0(decoder_1_out0[0]), .out1(decoder_1_out0[1]), .out2(decoder_1_out0[2]), .out3(decoder_1_out0[3]),
    .sel(multiplexer_1_out[1:0]));  // open: en
  assign and_8_out = out_6 & bit_extender_8_out;  // AND_Gate and_8, 32 bits wide
  assign wdata = and_3_out | and_5_out | and_4_out | and_6_out | and_8_out | and_7_out;  // OR_Gate or_3, 32 bits wide
  or or_4 (GPR_WE, comparator_7_eq, and_2_out, comparator_10_eq, comparator_6_eq, comparator_3_eq, comparator_4_eq);
  Adder #(.width(32)) adder_2 (.a(GPRs_rs1_val), .b(rs2_val), .out(add_result));  // open: cin, cout
  Multiplexer #(.width(32)) multiplexer_1 (
    .in0(addi_result), .in1(mwrite_addr),
    .out({multiplexer_1_out[31:18], ycoor, xcoor, multiplexer_1_out[1:0]}), .sel(does_write_memory));
  Comparator #(.width(10)) comparator_11 (.a(out_2), .b(10'h67), .eq(comparator_11_eq));  // open: gt, lt
  Multiplexer #(.width(4)) multiplexer_2 (.in0(4'b1111), .in1(decoder_1_out0), .out(multiplexer_2_out), .sel(is_sb));
  Multiplexer #(.width(32)) multiplexer_3 (
    .in0(rs2_val), .in1({rs2_val[7:0], rs2_val[7:0], rs2_val[7:0], rs2_val[7:0]}), .out(multiplexer_3_out),
    .sel(is_sb));
  Adder #(.width(32)) adder_3 (.a(bit_extender_7_out), .b(GPRs_rs1_val), .out(mwrite_addr));  // open: cin, cout
  Comparator #(.width(14)) comparator_12 (.a(14'h800), .b(multiplexer_1_out[31:18]), .eq(isVGA));  // open: gt, lt
  assign and_9_out = 32'hfffffffe & addi_result;  // AND_Gate and_9, 32 bits wide
  and and_10 (and_10_out, does_write_memory, comparator_13_eq);
  Comparator #(.width(6)) comparator_13 (
    .a({6{1'b0}}), .b(multiplexer_1_out[31:26]), .eq(comparator_13_eq));  // open: gt, lt
  RAM #(.addrWidth(24), .asyncread("true"), .byteenables("byteEnables"), .dataWidth(32), .\type ("nonvolatile")) ram_1 (
    .addr({multiplexer_1_out[25:18], ycoor, xcoor}), .we(and_10_out), .oe(1'b1), .clk(and_1_out),
    .din(multiplexer_3_out), .dout(out_6), .be3(multiplexer_2_out[3]), .be2(multiplexer_2_out[2]),
    .be1(multiplexer_2_out[1]), .be0(multiplexer_2_out[0]));
  Adder #(.width(32)) adder_4 (.a(PC_read), .b(32'h4), .out(out_3));  // open: cin, cout
  Multiplexer #(.width(32)) multiplexer_4 (.in0(out_3), .in1(and_9_out), .out(out_4), .sel(comparator_11_eq));
  GPR GPRs (
    .clk(and_1_out), .wdata(wdata), .R(R), .EN(GPR_WE), .rd(program_data[10:7]), .rs1(lui_result[18:15]),
    .rs2(lui_result[23:20]), .rs2_val(rs2_val), .rs1_val(GPRs_rs1_val));
  Multiplexer #(.select(2), .width(8)) multiplexer_5 (
    .in0(out_6[7:0]), .in1(out_6[15:8]), .in2(out_6[23:16]), .in3(out_6[31:24]), .out(multiplexer_5_out),
    .sel(multiplexer_1_out[1:0]));
  assign lbu_result = {{24{1'b0}}, multiplexer_5_out};  // Bit_Extender bit_extender_9
  // RGB_Video #(.cursor("No Cursor"), .height(256), .width(256)) rgb_video_1: pin names not known; wires that end beside it: R, and_1_out, isVGA, xcoor, ycoor, multiplexer_3_out[23:0]

  assign out_5 = out_4;

  // Other names for the same wires on the sheet: inst_type[9:0] = out_2; low_7_bits[6:0] = out_2[6:0];
  //   lui_result (some bits) = {high_7_bits, out_2[9:7]}; lw_result[31:0] = out_6; PC_write[31:0] = out_4

  // Notes on the sheet:
  //   R: initial=0xdd
  //   addi：imm[11:0][rs1]000[rd]0010011 加立即数
  //   add：0000000[rs2][rs1]000[rd]0110011 算术加法
  //   lui:imm[31:12][rd]0110111把立即数低位补0
  //   lw:imm[11:0][rs1]010[rd]0000011把rs1指示的内存32位加载到rd
  //   lbu:imm[11:0][rs1]100[rd]0000011把rs1所指的地址的8位加载到rd 0扩展
  //   sw:im[11:5][rs2][rs1]010imm[4:0]0100011 rs2加载到内存
  //   sb:im[11:5][rs2][rs1]000imm[4:0]0100011 rs2低8位加载到内存
  //   jalr:imm[11:0][rs1]000[rd]1100111把rs1+立即数的地址用于更新PC，同时把原PC+4写入rd
  //   byte addressable 每一个地址空间是一个字节
  //   contents of program (hex, n*v repeats v):
  //   413 93137 10113 10b7 dbc08093 80e7 fe012823 fea10923 fea12423 fe914203 fe4109a3 ff012783 f787b3
  //   f787b3 4b6b7 af868693 fdc10113 d787b3 10000713 f12423 10593 100793 b00513 2112023 12023 12223 e12623
  //   e12823 f10a23 10b7 a8408093 80e7 2012083 2410113 8067 ff410113 112423 10b7 a7c08093 80e7 513 1800093
  //   80e7 812083 513 c10113 8067 852583 feb12823 fe812e23 3437 80840413 ff014183 3401b3 1c183 ff114203
  //   440233 24203 4181b3 ff214203 440233 24203 4181b3 ff314203 440233 24203 4181b3 3237 80020213 320233
  //   24203 ffc12403 420233 420233 410233 11b7 86418193 fe312823 14800193 fe312623 fec22203 20067 1052703
  //   52683 452783 fe810113 e12423 112a23 812823 912623 fed12823 fef12623 13737 a0070713 fe012223 ff314203
  //   fe4102a3 fef14203 fe410223 fe412203 470233 24203 fe4105a3 ff214203 fe4102a3 fee14203 fe410223
  //   fe412203 470233 24203 fe410523 ff114203 fe4102a3 fed14203 fe410223 fe412203 470233 24203 fe4104a3
  //   ff014203 fe4102a3 fec14203 fe410223 fe412203 470233 24203 fe410423 fe812703 c52603 fee12823 fe812e23
  //   3437 80840413 ff014183 3401b3 1c183 ff114203 440233 24203 4181b3 ff214203 440233 24203 4181b3
  //   ff314203 440233 24203 4181b3 3237 80020213 320233 24203 ffc12403 420233 420233 410233 66800193
  //   fe312823 28800193 fe312623 fec22203 20067 c68733 10000513 fe812e23 fe912c23 fee12823 50413 ff012483
  //   fe812423 feb14183 3181b3 fe312423 fe914183 3181b3 fe912423 feb14203 420233 fe412423 fe914203 4181b3
  //   3181b3 fe312a23 fe912423 33237 90020213 feb14183 4181b3 1c183 fe3103a3 fea14183 4181b3 1c183
  //   fe310323 fe914183 4181b3 1c183 fe3102a3 fe814183 4181b3 1c183 fe310223 ff412183 fe412203 440233
  //   120213 fe412423 feb14203 420233 fe412423 fe914203 4181b3 3237 90820213 320233 ff812483 ffc12403
  //   24203 420233 420233 410233 11b7 86818193 fe312823 39000193 fe312623 fec22203 20067 812703 10000513
  //   e78733 fe812e23 fe912c23 fee12823 50413 ff012483 fe812423 feb14183 3181b3 fe312423 fe914183 3181b3
  //   fe912423 feb14203 420233 fe412423 fe914203 4181b3 3181b3 fe312a23 fe912423 33237 90020213 feb14183
  //   4181b3 1c183 fe3103a3 fea14183 4181b3 1c183 fe310323 fe914183 4181b3 1c183 fe3102a3 fe814183 4181b3
  //   1c183 fe310223 ff412183 fe412203 440233 120213 fe412423 feb14203 420233 fe412423 fe914203 4181b3
  //   3237 90820213 320233 ff812483 ffc12403 24203 420233 420233 410233 11b7 86818193 fe312823 49c00193
  //   fe312623 fec22203 20067 8*f787b3 d787b3 f787b3 f787b3 20000437 f40433 812783 c60633 c60633 fef12423
  //   feb14183 3181b3 fe312423 fe914183 fff78213 fe412423 feb14203 420233 fe412423 fe914203 4181b3 3237
  //   91820213 418233 24203 420233 420233 410233 65400193 fe312823 54000193 fe312623 fec22203 20067 493
  //   40513 b12223 c12023 10b7 de008093 80e7 12603 412583 812783 148493 40040413 c585b3 fef12823 fe912623
  //   fe812e23 fe912c23 2437 70040413 ff014183 340233 100193 320023 fec14183 3401b3 18023 24183 ff114483
  //   940233 100493 920023 fed14483 9404b3 48023 24483 9181b3 ff214483 940233 100493 920023 fee14483
  //   9404b3 48023 24483 9181b3 ff314483 940233 100493 920023 fef14483 9404b3 48023 24483 9181b3 3237
  //   80020213 320233 24203 ff812483 ffc12403 420233 420233 410233 65400193 fe312823 54400193 fe312623
  //   fec22203 20067 1412083 1012403 c12483 1810113 8067 10000713 fec12823 fee12623 fe812e23 fe912c23 2437
  //   70040413 ff014183 340233 100193 320023 fec14183 3401b3 18023 24183 ff114483 940233 100493 920023
  //   fed14483 9404b3 48023 24483 9181b3 ff214483 940233 100493 920023 fee14483 9404b3 48023 24483 9181b3
  //   ff314483 940233 100493 920023 fef14483 9404b3 48023 24483 9181b3 3237 80020213 320233 24203 ff812483
  //   ffc12403 420233 420233 410233 74c00193 fe312823 28800193 fe312623 fec22203 20067 812703 fee12823
  //   fec12623 fe812e23 fe912c23 2437 70040413 ff014183 340233 100193 320023 fec14183 3401b3 18023 24183
  //   ff114483 940233 100493 920023 fed14483 9404b3 48023 24483 9181b3 ff214483 940233 100493 920023
  //   fee14483 9404b3 48023 24483 9181b3 ff314483 940233 100493 920023 fef14483 9404b3 48023 24483 9181b3
  //   3237 80020213 320233 24203 ff812483 ffc12403 420233 420233 410233 11b7 83418193 fe312823 39000193
  //   fe312623 fec22203 20067 1012403 1412083 c12483 40637 20000537 1810113 1237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
  //   假设数据是低24位的
endmodule

module GPR (
  input  clk,
  input  [31:0] wdata,
  input  R,
  input  EN,
  input  [3:0] rd,
  input  [3:0] rs1,
  input  [3:0] rs2,
  output [31:0] rs2_val,
  output [31:0] rs1_val
);

  wire decoder_1_out0, decoder_1_out1, decoder_1_out2, decoder_1_out3, decoder_1_out4, decoder_1_out5,
       decoder_1_out6, decoder_1_out7, decoder_1_out8, decoder_1_out9, decoder_1_out10, decoder_1_out11,
       decoder_1_out12, decoder_1_out13, decoder_1_out14, decoder_1_out15;
  wire [31:0] register_1_q, register_2_q, register_3_q, register_4_q, register_5_q, register_6_q,
       register_7_q, register_8_q, register_9_q, register_10_q, register_11_q, register_12_q, register_13_q,
       register_14_q, register_15_q, register_16_q;

  Decoder #(.select(4)) decoder_1 (
    .out0(decoder_1_out0), .out1(decoder_1_out1), .out2(decoder_1_out2), .out3(decoder_1_out3),
    .out4(decoder_1_out4), .out5(decoder_1_out5), .out6(decoder_1_out6), .out7(decoder_1_out7),
    .out8(decoder_1_out8), .out9(decoder_1_out9), .out10(decoder_1_out10), .out11(decoder_1_out11),
    .out12(decoder_1_out12), .out13(decoder_1_out13), .out14(decoder_1_out14), .out15(decoder_1_out15),
    .sel(rd), .en(EN));
  Register #(.width(32)) register_1 (.D(wdata), .en(1'b0), .clk(clk), .Q(register_1_q), .clr(R));
  Register #(.width(32)) register_2 (.D(wdata), .en(decoder_1_out8), .clk(clk), .Q(register_2_q), .clr(R));
  Register #(.width(32)) register_3 (.D(wdata), .en(decoder_1_out1), .clk(clk), .Q(register_3_q), .clr(R));
  Register #(.width(32)) register_4 (.D(wdata), .en(decoder_1_out9), .clk(clk), .Q(register_4_q), .clr(R));
  Register #(.width(32)) register_5 (.D(wdata), .en(decoder_1_out2), .clk(clk), .Q(register_5_q), .clr(R));
  Register #(.width(32)) register_6 (.D(wdata), .en(decoder_1_out10), .clk(clk), .Q(register_6_q), .clr(R));
  Register #(.width(32)) register_7 (.D(wdata), .en(decoder_1_out3), .clk(clk), .Q(register_7_q), .clr(R));
  Register #(.width(32)) register_8 (.D(wdata), .en(decoder_1_out11), .clk(clk), .Q(register_8_q), .clr(R));
  Register #(.width(32)) register_9 (.D(wdata), .en(decoder_1_out4), .clk(clk), .Q(register_9_q), .clr(R));
  Register #(.width(32)) register_10 (.D(wdata), .en(decoder_1_out12), .clk(clk), .Q(register_10_q), .clr(R));
  Register #(.width(32)) register_11 (.D(wdata), .en(decoder_1_out5), .clk(clk), .Q(register_11_q), .clr(R));
  Register #(.width(32)) register_12 (.D(wdata), .en(decoder_1_out13), .clk(clk), .Q(register_12_q), .clr(R));
  Register #(.width(32)) register_13 (.D(wdata), .en(decoder_1_out6), .clk(clk), .Q(register_13_q), .clr(R));
  Register #(.width(32)) register_14 (.D(wdata), .en(decoder_1_out14), .clk(clk), .Q(register_14_q), .clr(R));
  Register #(.width(32)) register_15 (.D(wdata), .en(decoder_1_out7), .clk(clk), .Q(register_15_q), .clr(R));
  Register #(.width(32)) register_16 (.D(wdata), .en(decoder_1_out15), .clk(clk), .Q(register_16_q), .clr(R));
  Multiplexer #(.select(4), .width(32)) multiplexer_1 (
    .in0(register_1_q), .in1(register_3_q), .in2(register_5_q), .in3(register_7_q), .in4(register_9_q),
    .in5(register_11_q), .in6(register_13_q), .in7(register_15_q), .in8(register_2_q), .in9(register_4_q),
    .in10(register_6_q), .in11(register_8_q), .in12(register_10_q), .in13(register_12_q),
    .in14(register_14_q), .in15(register_16_q), .out(rs2_val), .sel(rs2));
  Multiplexer #(.select(4), .width(32)) multiplexer_2 (
    .in0(register_1_q), .in1(register_3_q), .in2(register_5_q), .in3(register_7_q), .in4(register_9_q),
    .in5(register_11_q), .in6(register_13_q), .in7(register_15_q), .in8(register_2_q), .in9(register_4_q),
    .in10(register_6_q), .in11(register_8_q), .in12(register_10_q), .in13(register_12_q),
    .in14(register_14_q), .in15(register_16_q), .out(rs1_val), .sel(rs1));
endmodule
